# Fritzing sketch 2025 FRC 2491 Season Diagram (saved by Fritzing 0.9.3b)

parts:
  RPM1 = Pigeon
  CANivore1 = CANivore
  cntl1 = roborio_v2
  BAT1 = Battery 12V [package=battcom_20mm_pth]
  CB1 = Thermal Circuit Breaker [package=waterproof]
  RPM2 = rev_rpm
  Router1 = Rounter OpenMesh
  PDH1 = rev_pdh
  JP1 = APP SB50 [package=sb50]
  JP2 = APP SB50 [package=sb50]
  Part1 = WCP_Kraken_X60 [part_number=19-708850]
  BLDC1 = CTRE Falcon 500 [part_number=19-708850]
  Connector1 = CANcoder
  Part2 = WCP_Kraken_X60 [part_number=19-708850]
  BLDC2 = CTRE Falcon 500 [part_number=19-708850]
  Connector3 = CANcoder
  Part3 = WCP_Kraken_X60 [part_number=19-708850]
  BLDC3 = CTRE Falcon 500 [part_number=19-708850]
  Connector4 = CANcoder
  Part4 = WCP_Kraken_X60 [part_number=19-708850]
  BLDC4 = CTRE Falcon 500 [part_number=19-708850]
  Connector5 = CANcoder
  Connector6 = Quad Connecotr
  Connector7 = Wago Connector
  Connector8 = Wago Connector
  Connector9 = Wago Connector
  Connector10 = Wago Connector
  Connector11 = Wago Connector
  Connector12 = Wago Connector
  Fuse2 = 40A PDH Breaker
  Fuse3 = 40A PDH Breaker
  Fuse4 = 40A PDH Breaker
  Fuse5 = 40A PDH Breaker
  R1 = Resistor [tolerance=±5% resistance=220 package="2512 [SMD]"]
  Connector13 = Wago Connector
  Connector14 = Wago Connector
  Connector15 = Wago Connector
  Connector16 = Wago Connector
  Connector17 = Wago Connector
  Connector18 = Wago Connector
  Fuse6 = 40A PDH Breaker
  Fuse7 = 40A PDH Breaker
  Fuse8 = 40A PDH Breaker
  Fuse9 = 40A PDH Breaker
  RSL2 = FRC Robot Signal Light [part_number=855PB-B12ME522]

nets:
  N1: RPM1.connector0, Connector8.connector0
  N2: RPM1.connector1, Connector7.connector0
  N3: RPM1.connector2, BLDC1.CANH1#5
  N4: RPM1.connector3, BLDC1.CANL1
  N5: RPM1.connector4, Part4.CAN_Y_2
  N6: RPM1.connector5, Part4.CAN_G_2
  N7: CANivore1.connector0, Connector10.connector0
  N8: CANivore1.connector1, Connector9.connector0
  N9: CANivore1.connector2, Connector6.connector3
  N10: CANivore1.connector3, Connector6.connector4
  N11: CANivore1.connector4, cntl1.connector142
  N12: cntl1.connector41, RSL2.common_cathode
  N13: cntl1.connector42, RSL2.anode0, RSL2.anode1
  N14: cntl1.connector144, RPM2.connector3
  N15: BAT1.+, JP1.2
  N16: BAT1.-, JP1.1
  N17: CB1.1, PDH1.connector45
  N18: CB1.2, JP2.2
  N19: RPM2.connector0, PDH1.connector52
  N20: RPM2.connector1, PDH1.connector53
  N21: RPM2.connector2, Router1.ETH_right
  N22: PDH1.connector0, Connector12.connector1
  N23: PDH1.connector1, Connector11.connector1
  N24: PDH1.connector2, Part3.Vin+
  N25: PDH1.connector3, Part3.Vin-
  N26: PDH1.connector4, Connector16.connector1
  N27: PDH1.connector5, Connector15.connector1
  N28: PDH1.connector6, Part2.Vin+
  N29: PDH1.connector7, Part2.Vin-
  N30: PDH1.connector32, Connector13.connector1
  N31: PDH1.connector33, Connector14.connector1
  N32: PDH1.connector34, Part1.Vin-
  N33: PDH1.connector35, Part1.Vin+
  N34: PDH1.connector36, Connector18.connector0
  N35: PDH1.connector37, Connector17.connector0
  N36: PDH1.connector38, Part4.Vin-
  N37: PDH1.connector39, Part4.Vin+
  N38: PDH1.connector44, JP2.1
  N39: PDH1.connector46, Connector8.connector1
  N40: PDH1.connector47, Connector7.connector1
  N41: PDH1.connector48, Connector10.connector1
  N42: PDH1.connector49, Connector9.connector1
  N43: PDH1.connector54, Fuse7.connector0
  N44: PDH1.connector55, Fuse3.connector0
  N45: PDH1.connector56, Fuse8.connector0
  N46: PDH1.connector57, Fuse2.connector0
  N47: PDH1.connector70, Fuse9.connector0
  N48: PDH1.connector71, Fuse5.connector0
  N49: PDH1.connector72, Fuse6.connector0
  N50: PDH1.connector73, Fuse4.connector0
  N51: Part1.CAN_Y_1, R1.Pin_0
  N52: Part1.CAN_G_1, R1.Pin_1
  N53: Part1.CAN_Y_2, BLDC1.CANH1#3, Connector1.connector3
  N54: Part1.CAN_G_2, BLDC1.CANL0, Connector1.connector4
  N55: Part1.Middle_Connector_Pin_Power_Out_Red, Connector1.connector1
  N56: Part1.Middle_Connector_Pin_Power_Out_Black, Connector1.connector0
  N57: BLDC1.Vin-, Connector13.connector0
  N58: BLDC1.Vin+, Connector14.connector0
  N59: Part2.CAN_Y_1, BLDC3.CANH1#5
  N60: Part2.CAN_G_1, BLDC3.CANL1
  N61: Part2.CAN_Y_2, BLDC2.CANH1#5, Connector3.connector3
  N62: Part2.CAN_G_2, BLDC2.CANL1, Connector3.connector4
  N63: Part2.Middle_Connector_Pin_Power_Out_Red, Connector3.connector1
  N64: Part2.Middle_Connector_Pin_Power_Out_Black, Connector3.connector0
  N65: BLDC2.Vin-, Connector15.connector0
  N66: BLDC2.Vin+, Connector16.connector0
  N67: BLDC2.CANL0, Connector6.connector1
  N68: BLDC2.CANH1#3, Connector6.connector0
  N69: Part3.CAN_Y_1, BLDC4.CANH1#5
  N70: Part3.CAN_G_1, BLDC4.CANL1
  N71: Part3.CAN_Y_2, BLDC3.CANH1#3, Connector4.connector3
  N72: Part3.CAN_G_2, BLDC3.CANL0, Connector4.connector4
  N73: Part3.Middle_Connector_Pin_Power_Out_Red, Connector4.connector1
  N74: Part3.Middle_Connector_Pin_Power_Out_Black, Connector4.connector0
  N75: BLDC3.Vin-, Connector11.connector0
  N76: BLDC3.Vin+, Connector12.connector0
  N77: Part4.CAN_Y_1, BLDC4.CANH1#3, Connector5.connector3
  N78: Part4.CAN_G_1, BLDC4.CANL0, Connector5.connector4
  N79: Part4.Middle_Connector_Pin_Power_Out_Red, Connector5.connector1
  N80: Part4.Middle_Connector_Pin_Power_Out_Black, Connector5.connector0
  N81: BLDC4.Vin-, Connector18.connector1
  N82: BLDC4.Vin+, Connector17.connector1

notes:
  back right
  back left
  120 OHM Resistor
  front left
  front right
  Lb into La

custom parts:
  Battery 12V: Battery Holders Various common sizes : AA, AAA, 20mm coin cell and 12mm coin cell.
  Thermal Circuit Breaker: Cooper Bussman P/N CB185-120, CB185F-120, CB285-120 CB285F-120, CB285120F or Optifuse P/N 153120, 253120
  APP SB50: Anderson Power Products SB®50 Connectors feature a one-piece plastic housing using stainless steel springs to hold low-resistance contacts in place. These connectors work with wire contacts up to 6AWG (10mm²) as well as PCB and busbar contacts. The genderless design mates with itself and has a plated through-hole mounting style. Anderson SB®50 Connectors are UL-rated for hot plugging up to 50A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
  WCP_Kraken_X60: The Kraken X60 is a brushless motor developed by WestCoast Products that has been designed to withstand the rigors of the FIRST Robotics Competition.
  CTRE Falcon 500: The Falcon 500 powered by Talon FX is a brushless motor with an integrated motor controller and high-resolution encoder, custom designed specifically for the FIRST Robotics Competition, through a collaboration between Cross the Road Electronics and VEX Robotics.
  FRC Robot Signal Light: Panel Mount Beacon,12V AC/DC,45 mm Panel Mounting LED,Amber,22.5 mm Round Mounting Hole Used as: R709 *ROBOTS must have a signal light. ROBOTS must use at least 1, but no more than 2, diagnostic ROBOT Signal Light (RSL) (P/N 855PB-B12ME522). Any RSL must be: A. mounted on the ROBOT such that it is easily visible while standing 3 ft. (~ 100 cm) in front of the ROBOT, B. connected to the “RSL”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
